# Fritzing sketch Sensor assignment 3 (saved by Fritzing 0.9.3b)
breadboards: 2

parts:
  M1 = DOIT Esp32 DevKit v1 (30 pins long, 11 pins width) [part_number=ESP32S-PIN30]
  DHT1 = DHT11 Humitidy and Temperature Sensor (3 pins)
  A1 = MQ-2 breakout
  KF-1 = KF-301 Relay [package=THT]
  OLED_I2C1 = OLED 128x64 I2C Monochrome Display
  e-radionica_com1 = LM393 LDR breakout [part_number=100027]
  FC-1 = Sound Sensor
  buz1 = Piezo Buzzer
  S1 = SWITCH-DPDT-latching [package=os]

nets:
  VCC: M1.3V3, DHT1.Plus, KF-1.power, OLED_I2C1.VDD, e-radionica_com1.VCC, FC-1.VCC
  GND: M1.GND, DHT1.Gnd, A1.GND, KF-1.ground, OLED_I2C1.GND, e-radionica_com1.GND, FC-1.GND, buz1.pin_1, S1.1
  N1: M1.D4, DHT1.Signal
  N2: M1.D21, OLED_I2C1.SDA
  N3: M1.D22, OLED_I2C1.SCK
  N4: M1.D34, A1.AO
  N5: M1.D35, e-radionica_com1.AO
  N6: M1.D32, FC-1.OUT
  N7: M1.D25, S1.3
  N8: M1.D26, buz1.pin_2
  N9: M1.D14, KF-1.signal
  VIN: M1.VIN, A1.VCC

notes:
  DHT11
  + -> 3V3
  out -> D4
  - -> GND
  OLED
  GND -> GND
  VCC -> 3V3
  SCL -> D22
  SDA -> D21
  LDR
  VCC -> 3V3
  GND -> GND
  DO -> D35
  Sound Sensor
  VCC -> 3V3
  GND -> GND
  OUT -> D32
  MQ-2
  VCC -> 5V
  GND -> GND
  AO -> D34
  Relay
  VCC ->3.3V
  GND -> GND
  IN -> D14
  Button
  One side -> D27
  Other side -> GND
  Mode: INPUT_PULLUP
  Buzzer
  + -> D26
  - -> GND
  Power Rails
  Blue rails -> Common GND
  Bottom red rail -> 3V3: DHT11, OLED, LDR, Sound
  Top red rail -> 5V/VIN: MQ-2, Relay

custom parts:
  DOIT Esp32 DevKit v1 (30 pins long, 11 pins width): The DOIT Esp32 DevKit v1 is one of the development board created by DOIT to evaluate the ESP-WROOM-32 module. It is based on the ESP32 microcontroller that boasts Wifi, Bluetooth, Ethernet and Low Power support all in a single chip. (vanepp) made breadboard work, adjusted pin numbering and labels and reduced size of schematic and cleaned up pcb. This chip is 30pins long (2 x15) and 11 pins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
  DHT11 Humitidy and Temperature Sensor (3 pins): DHT11 Humidity and Temperature Sensor (3 pins).
  MQ-2 breakout: MQ-2 gas sensor
  KF-301 Relay: KF-301
  Piezo Buzzer: Part from https://www.nutsvolts.com/magazine/article/november2012_SmileysWorkshop modified to be .3 in spacing to match the adafruit buzzer 5V breadboard friendly part.
  SWITCH-DPDT-latching: DPDT latching pushbutton switch
